// Digital circuit ULA.dig as structural Verilog
module ULA (
  input  A,
  input  B
);

  NOT not_1 ();  // open: A, S
  XOR xor_1 ();  // open: A, B, S
  OR or_1 ();  // open: A, B, S
  AND and_1 ();  // open: A, B, S
endmodule
